// Logisim project CPU.circ as structural Verilog: 3 circuits, main circuit main
module main (
);

  wire clock_2_clock_status, clock_2_value, Clock_out, Clock_Select_out, pull_resistor_1_node, Step_out;

  Clock_part Clock (.out(Clock_out));
  Button Clock_Select (.out(Clock_Select_out));
  LED Clock_Status (.in(clock_2_clock_status));
  Button Step (.out(Step_out));
  Clock clock_2 (
    .Clock(Clock_out), .Clock_Select(Clock_Select_out), .Clock_Status(clock_2_clock_status), .Step(Step_out),
    .Halt(pull_resistor_1_node), .Value(clock_2_value));
  Pull_Resistor pull_resistor_1 (.node(pull_resistor_1_node));
  LED Clock_Throughput (.in(clock_2_value));

  // Notes on the sheet:
  //   TODO : Make a custom D Flip Flop
endmodule

module Clock (
  input  Clock,
  input  Clock_Select,
  input  Step,
  input  Halt,
  output Value,
  output Clock_Status
);

  wire and_1_out, and_2_out, not_1_out, not_2_out, or_1_out;

  Switch Switch (.Switch_Toggle(Clock_Select), .Switch_Value(Clock_Status));
  not not_1 (not_1_out, Halt);
  and and_1 (and_1_out, Clock, Clock_Status);
  and and_2 (and_2_out, Step, not_2_out);
  not not_2 (not_2_out, Clock_Status);
  or or_1 (or_1_out, and_1_out, and_2_out);
  and u_Halt (Value, or_1_out, not_1_out);

  // Notes on the sheet:
  //   1 = ON, 0 = OFF
  //   When Step is triggered, it will
  //   advance the clock 1 tick
endmodule

module Switch (
  input  Switch_Toggle,
  output Switch_Value
);

  wire d_ff_1_qn;

  D_Flip_Flop d_ff_1 (.clk(Switch_Toggle), .D(d_ff_1_qn), .Q(Switch_Value), .Qn(d_ff_1_qn));  // open: preset, en, reset
endmodule
